# Fritzing sketch Photobioreactor - Fritzing (saved by Fritzing 0.9.2b)
breadboards: 1

parts:
  Part1 = Arduino Leonardo (Rev3b)
  LCD2 = LCD screen
  LCM1602_IIC3 = LCM1602 IIC [part_number="LCM1602 IIC" chip_label="LCM1602 IIC" package="DIP (Dual Inline) [THT]"]
  Part2 = Adafruit TSL2561 [part_number="Adafruit #439"]
  WhiteLEDmodule1 = WhiteLEDmodule
  R1 = Temperature Sensor (Thermistor) [thermistor_type=NTC package=THT]
  R2 = Resistor [tolerance=±5% resistance=10k package=THT]
  KY-5 = Keyes Relay [package=THT]
  KY-6 = Keyes Relay [package=THT]

nets:
  N1: Part1.D2/SDA, Part1.SDA, LCM1602_IIC3.SDA, Part2.SDA
  N2: Part1.D3_PWM/SCL, Part1.SCL, LCM1602_IIC3.SCL, Part2.SCL
  N3: Part1.D6_PWM/A7, KY-5.signal
  5V: Part1.5V, LCM1602_IIC3.VCC, Part2.VIN, WhiteLEDmodule1.POWER, R1.pin_0, KY-5.power
  GND: Part1.GND, LCM1602_IIC3.GND, Part2.GND, WhiteLEDmodule1.GND, R2.Pin_0, KY-5.ground
  N4: Part1.VIN, KY-5.C
  N5: Part1.A0, WhiteLEDmodule1.INPUT
  N6: Part1.A1, R1.pin_1, R2.Pin_1
  VSS: LCD2.VSS, LCM1602_IIC3.VSS
  VDD: LCD2.VDD, LCM1602_IIC3.VDD
  N7: LCD2.V0, LCM1602_IIC3.V0
  N8: LCD2.RS, LCM1602_IIC3.RS
  N9: LCD2.R/W, LCM1602_IIC3.RW
  N10: LCD2.E, LCM1602_IIC3.E
  N11: LCD2.DB0, LCM1602_IIC3.D0
  N12: LCD2.DB1, LCM1602_IIC3.D1
  N13: LCD2.DB2, LCM1602_IIC3.D2
  N14: LCD2.DB3, LCM1602_IIC3.D3
  N15: LCD2.DB4, LCM1602_IIC3.D4
  N16: LCD2.DB5, LCM1602_IIC3.D5
  N17: LCD2.DB6, LCM1602_IIC3.D6
  N18: LCD2.DB7, LCM1602_IIC3.D7
  N19: LCD2.LED+, LCM1602_IIC3.A
  N20: LCD2.LED-, LCM1602_IIC3.K
  N21: LCM1602_IIC3.LED_A, LCM1602_IIC3.LED_B
  N22: KY-5.NO, KY-6.NC, KY-6.C

notes:
  LCD SCREEN
  This panel is already soldered to the back of the LCD screen.
  Please note the abbreviations next to each pin
  Temperature Sensor
  pH Sensor
  Digital light sensor
  Arduino Leonardo
  Relay board
  LED connector
  LCD + LCD controller
  Relay

custom parts:
  LCM1602 IIC: I2C-Module to use a 1602 or 2004 LCD on with the wire.h libory Serial LCD Modul
  Adafruit TSL2561: The TSL2561 luminosity sensor is an advanced digital light sensor, ideal for use in a wide range of light situations. Compared to low cost CdS cells, this sensor is more precise, allowing for exact lux calculations and can be configured for different gain/timing ranges to detect light ranges from up to 0.1 - 40,000+ Lux on the fly. The best part of this sensor is that it contains both infrared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
  Keyes Relay: The Keyes 5V relay module is suitable for SCM development, home appliance control. It uses a 5V~12V TIL control signal which can control DC / AC signal.
